# Fritzing sketch digital-temp-DS18B20 (saved by Fritzing 0.7.12b)
breadboards: 1

parts:
  +_- = mystery part, 2 pins [chip_label=PWR-IN]
  d_c = mystery part, 2 pins [chip_label=DATA-IN]
  +_-_2 = mystery part, 2 pins [chip_label=PWR-OUT]
  d_c_2 = mystery part, 2 pins [chip_label=DATA-OUT]
  R2 = Resistor [tolerance=±5% resistance=10k package="0805 [SMD]"]
  PWR = smd LED [color="Red (633nm)" package="0805 [SMD]"]
  C1 = Tantalum Capacitor [capacitance="1 μF" package="A 3216 [SMD, tantalum]"]
  Temperature = mystery part, 3 pins [chip_label=?]
  PWR1 = smd LED [color="Red (633nm)" package="0805 [SMD]"]

nets:
  N1: +_-.pin1, +_-_2.pin2, PWR.cathode, C1.-, Temperature.pin1
  N2: +_-.pin2, +_-_2.pin1, R2.Pin_1, C1.+, Temperature.pin3, PWR1.anode
  N3: d_c.pin1, d_c_2.pin2
  N4: d_c.pin2, Temperature.pin2, PWR1.cathode
  N5: R2.Pin_0, PWR.anode

notes:
  In this example, a pushbutton is used as a digital input and an LED is a digital output. Related example: http://arduino.cc/en/Tutorial/Button
  DS18B20
